# Fritzing sketch jiin_Speaker (saved by Fritzing 0.9.3b)
breadboards: 1

parts:
  부품1 = Arduino Uno (Rev3)
  J1 = Piezo Speaker

nets:
  N1: 부품1.5V, J1.pin2
  N2: 부품1.GND, J1.pin1

// code stored in the sketch: jiin_Speaker.code.ino
void setup()
{
  int melody[] = {262, 294, 330, 349, 392, 440, 492};  
  for(int i = 0; i<7; i++){
    tone(8, melody[i], 500); delay(500);
  }
}

void loop()
{
  digitalWrite(13, HIGH);
  delay(1000); // Wait for 1000 millisecond(s)
  digitalWrite(13, LOW);
  delay(1000); // Wait for 1000 millisecond(s)
}
